// Logisim project adder.circ as structural Verilog: 1 circuit, main circuit CombinationalAdder
module CombinationalAdder (
  input  [7:0] A,
  input  [7:0] B,
  output [7:0] S
);

  Adder #(.width(8)) adder_1 (.a(A), .b(B), .out(S));  // open: cin, cout
endmodule
