// Logisim project course-multi-ram.circ as structural Verilog: 1 circuit, main circuit main
module main (
  input  reset,
  output [31:0] Instr,
  output [31:0] pc,
  output RegWrite,
  output [4:0] RegAddr,
  output [31:0] RegData,
  output MemWrite,
  output [31:0] MemAddr,
  output [31:0] MemData
);

  wire ALUOP0, ALUOP1, ALUSRC, CLK, CLK1, CLKCPU, DEC0, DEC1, DEC2, DEC3, DEC4, DEC5, DEC6, DEC7, DEC8, DEC9,
       DEC10, DEC11, DEC12, DEC13, DEC14, DEC15, DEC16, DEC17, DEC18, DEC19, DEC20, DEC21, DEC22, DEC23,
       DEC24, DEC25, DEC26, DEC27, DEC28, DEC29, DEC30, DEC31, EN0, EN1, EN2, EN3, EN4, EN5, EN6, EN7, EN8,
       EN9, EN10, EN11, EN12, EN13, EN14, EN15, EN16, EN17, EN18, EN19, EN20, EN21, EN22, EN23, EN24, EN25,
       EN26, EN27, EN28, EN29, EN30, EN31, EQ, IS_ADD, IS_ADD_F, IS_BEQ, IS_J, IS_LUI, IS_LW, IS_ORI, IS_R,
       IS_SLL, IS_SLL_F, IS_SUB, IS_SUB_F, IS_SW, REGWE, REGWRITE_t, TAKEN, WRITENOTZERO, WRITEZERO;
  wire [4:0] WRITEADDR;
  wire [5:0] FUNCT;
  wire [11:0] PCINDEX;
  wire [15:6] IMM16;
  wire [31:0] ADDSUB, ADDSUM, ALU_HI, ALUA, ALUB, ALUOUT, BRANCHTARGET, IMMEXT, JINDEX32, JSHIFTED, JTARGET,
       LOADDATA, LUI_VALUE, NEXTPC, OROUT, PC4, PC_HIGH, PC_t, PCBRANCH, PCD, PCOFFSET, R0, R1, R2, R3, R4,
       R5, R6, R7, R8, R9, R10, R11, R12, R13, R14, R15, R16, R17, R18, R19, R20, R21, R22, R23, R24, R25,
       R26, R27, R28, R29, R30, R31, REGRESULT, REGRESULT_BASE, RSVALUE, RTVALUE, SHIFTEDOFFSET, SIGNIMM,
       SLLOUT, SUBSUM, ZEROIMM;
  wire [31:16] INSTR_t;

  not not_1 (CLK1, CLK);
  Multiplexer #(.width(32), .select(1), .enable("false")) multiplexer_1 (
    .in0(NEXTPC), .in1(32'h3000), .out(PCD), .sel(reset));
  Decoder #(.select(5), .enable("false")) decoder_1 (
    .out0(DEC0), .out1(DEC1), .out2(DEC2), .out3(DEC3), .out4(DEC4), .out5(DEC5), .out6(DEC6), .out7(DEC7),
    .out8(DEC8), .out9(DEC9), .out10(DEC10), .out11(DEC11), .out12(DEC12), .out13(DEC13), .out14(DEC14),
    .out15(DEC15), .out16(DEC16), .out17(DEC17), .out18(DEC18), .out19(DEC19), .out20(DEC20), .out21(DEC21),
    .out22(DEC22), .out23(DEC23), .out24(DEC24), .out25(DEC25), .out26(DEC26), .out27(DEC27), .out28(DEC28),
    .out29(DEC29), .out30(DEC30), .out31(DEC31), .sel(WRITEADDR));
  and and_1 (EN1, DEC1, REGWE);
  and and_2 (EN4, DEC4, REGWE);
  and and_3 (EN7, DEC7, REGWE);
  and and_4 (EN10, DEC10, REGWE);
  and and_5 (EN13, DEC13, REGWE);
  and and_6 (EN16, DEC16, REGWE);
  and and_7 (EN19, DEC19, REGWE);
  and and_8 (EN22, DEC22, REGWE);
  and and_9 (EN25, DEC25, REGWE);
  and and_10 (EN28, DEC28, REGWE);
  and and_11 (EN31, DEC31, REGWE);
  Comparator #(.width(6), .mode("unsigned")) comparator_1 (
    .a(INSTR_t[31:26]), .b(6'b001111), .eq(IS_LUI));  // open: gt, lt
  Comparator #(.width(6), .mode("unsigned")) comparator_2 (.a(FUNCT), .b(6'b100010), .eq(IS_SUB_F));  // open: gt, lt
  or or_1 (ALUOP0, IS_SUB, IS_SLL);
  assign ZEROIMM = {{16{1'b0}}, {IMM16, FUNCT}};  // Bit_Extender bit_extender_1
  Subtractor #(.width(32)) subtractor_1 (.a(ALUA), .b(ALUB), .out(SUBSUM), .bin(1'b0));  // open: bout
  RAM #(.addrWidth(12), .dataWidth(32), .bus("separate")) DATA_RAM (
    .addr(ALUOUT[13:2]), .din(RTVALUE), .data(LOADDATA), .str(IS_SW), .sel(1'b1), .clk(CLK), .ld(IS_LW),
    .clr(reset));
  assign PC_HIGH = PC4 & 32'hf0000000;  // AND_Gate and_12, 32 bits wide
  buf buffer_1 (RegWrite, REGWE);
  Clock #(.highDuration(1), .lowDuration(1)) clock_1 (.out(CLK));
  not not_2 (CLKCPU, CLK1);
  Register #(.width(32)) PC_REG (.D(PCD), .en(1'b1), .Q(PC_t), .clk(CLKCPU), .clr(1'b0));
  Comparator #(.width(5), .mode("unsigned")) comparator_3 (
    .a(WRITEADDR), .b({5{1'b0}}), .eq(WRITEZERO));  // open: gt, lt
  Register #(.width(32)) register_1 (.D(REGRESULT), .en(EN1), .Q(R1), .clk(CLKCPU), .clr(reset));
  Register #(.width(32)) register_2 (.D(REGRESULT), .en(EN4), .Q(R4), .clk(CLKCPU), .clr(reset));
  Register #(.width(32)) register_3 (.D(REGRESULT), .en(EN7), .Q(R7), .clk(CLKCPU), .clr(reset));
  Register #(.width(32)) register_4 (.D(REGRESULT), .en(EN10), .Q(R10), .clk(CLKCPU), .clr(reset));
  Register #(.width(32)) register_5 (.D(REGRESULT), .en(EN13), .Q(R13), .clk(CLKCPU), .clr(reset));
  Register #(.width(32)) register_6 (.D(REGRESULT), .en(EN16), .Q(R16), .clk(CLKCPU), .clr(reset));
  Register #(.width(32)) register_7 (.D(REGRESULT), .en(EN19), .Q(R19), .clk(CLKCPU), .clr(reset));
  Register #(.width(32)) register_8 (.D(REGRESULT), .en(EN22), .Q(R22), .clk(CLKCPU), .clr(reset));
  Register #(.width(32)) register_9 (.D(REGRESULT), .en(EN25), .Q(R25), .clk(CLKCPU), .clr(reset));
  Register #(.width(32)) register_10 (.D(REGRESULT), .en(EN28), .Q(R28), .clk(CLKCPU), .clr(reset));
  Register #(.width(32)) register_11 (.D(REGRESULT), .en(EN31), .Q(R31), .clk(CLKCPU), .clr(reset));
  Comparator #(.width(6), .mode("unsigned")) comparator_4 (
    .a(INSTR_t[31:26]), .b(6'b001101), .eq(IS_ORI));  // open: gt, lt
  Comparator #(.width(6), .mode("unsigned")) comparator_5 (.a(FUNCT), .b({6{1'b0}}), .eq(IS_SLL_F));  // open: gt, lt
  or or_2 (ALUOP1, IS_ORI, IS_SLL);
  Multiplexer #(.width(32), .select(1), .enable("false")) multiplexer_2 (
    .in0(SIGNIMM), .in1(ZEROIMM), .out(IMMEXT), .sel(IS_ORI));
  assign OROUT = ALUA | ALUB;  // OR_Gate or_3, 32 bits wide
  assign JTARGET = PC_HIGH | JSHIFTED;  // OR_Gate or_4, 32 bits wide
  assign RegAddr = WRITEADDR;  // Buffer buffer_2, 5 bits wide
  Adder #(.width(32)) adder_1 (.a(PC_t), .b(32'h4), .out(PC4), .cin(1'b0));  // open: cout
  not not_3 (WRITENOTZERO, WRITEZERO);
  and and_13 (EN2, DEC2, REGWE);
  and and_14 (EN5, DEC5, REGWE);
  and and_15 (EN8, DEC8, REGWE);
  and and_16 (EN11, DEC11, REGWE);
  and and_17 (EN14, DEC14, REGWE);
  and and_18 (EN17, DEC17, REGWE);
  and and_19 (EN20, DEC20, REGWE);
  and and_20 (EN23, DEC23, REGWE);
  and and_21 (EN26, DEC26, REGWE);
  and and_22 (EN29, DEC29, REGWE);
  Multiplexer #(.width(32), .select(5), .enable("false")) multiplexer_3 (
    .in0(R0), .in1(R1), .in2(R2), .in3(R3), .in4(R4), .in5(R5), .in6(R6), .in7(R7), .in8(R8), .in9(R9),
    .in10(R10), .in11(R11), .in12(R12), .in13(R13), .in14(R14), .in15(R15), .in16(R16), .in17(R17),
    .in18(R18), .in19(R19), .in20(R20), .in21(R21), .in22(R22), .in23(R23), .in24(R24), .in25(R25),
    .in26(R26), .in27(R27), .in28(R28), .in29(R29), .in30(R30), .in31(R31), .out(RSVALUE),
    .sel(INSTR_t[25:21]));
  Comparator #(.width(6), .mode("unsigned")) comparator_6 (
    .a(INSTR_t[31:26]), .b(6'b100011), .eq(IS_LW));  // open: gt, lt
  and and_23 (IS_ADD, IS_R, IS_ADD_F);
  or or_5 (ALUSRC, IS_ORI, IS_LW, IS_SW);
  Shifter #(.width(32), .shift("ll")) shifter_1 (.in(ZEROIMM), .\dist (5'b10000), .out(LUI_VALUE));
  Shifter #(.width(32), .shift("ll")) shifter_2 (.in(ALUA), .\dist (IMM16[10:6]), .out(SLLOUT));
  Multiplexer #(.width(32), .select(1), .enable("false")) multiplexer_4 (
    .in0(ALUOUT), .in1(LOADDATA), .out(REGRESULT_BASE), .sel(IS_LW));
  Multiplexer #(.width(32), .select(1), .enable("false")) multiplexer_5 (
    .in0(PC4), .in1(BRANCHTARGET), .out(PCBRANCH), .sel(TAKEN));
  assign RegData = REGRESULT;  // Buffer buffer_3, 32 bits wide
  Subtractor #(.width(32)) subtractor_2 (
    .a(PC_t), .b(32'h3000), .out({PCOFFSET[31:14], PCINDEX, PCOFFSET[1:0]}), .bin(1'b0));  // open: bout
  assign JINDEX32 = {{6{1'b0}}, {INSTR_t[25:16], IMM16, FUNCT}};  // Bit_Extender bit_extender_2
  and and_24 (REGWE, REGWRITE_t, WRITENOTZERO);
  Register #(.width(32)) register_12 (.D(REGRESULT), .en(EN2), .Q(R2), .clk(CLKCPU), .clr(reset));
  Register #(.width(32)) register_13 (.D(REGRESULT), .en(EN5), .Q(R5), .clk(CLKCPU), .clr(reset));
  Register #(.width(32)) register_14 (.D(REGRESULT), .en(EN8), .Q(R8), .clk(CLKCPU), .clr(reset));
  Register #(.width(32)) register_15 (.D(REGRESULT), .en(EN11), .Q(R11), .clk(CLKCPU), .clr(reset));
  Register #(.width(32)) register_16 (.D(REGRESULT), .en(EN14), .Q(R14), .clk(CLKCPU), .clr(reset));
  Register #(.width(32)) register_17 (.D(REGRESULT), .en(EN17), .Q(R17), .clk(CLKCPU), .clr(reset));
  Register #(.width(32)) register_18 (.D(REGRESULT), .en(EN20), .Q(R20), .clk(CLKCPU), .clr(reset));
  Register #(.width(32)) register_19 (.D(REGRESULT), .en(EN23), .Q(R23), .clk(CLKCPU), .clr(reset));
  Register #(.width(32)) register_20 (.D(REGRESULT), .en(EN26), .Q(R26), .clk(CLKCPU), .clr(reset));
  Register #(.width(32)) register_21 (.D(REGRESULT), .en(EN29), .Q(R29), .clk(CLKCPU), .clr(reset));
  Multiplexer #(.width(32), .select(5), .enable("false")) multiplexer_6 (
    .in0(R0), .in1(R1), .in2(R2), .in3(R3), .in4(R4), .in5(R5), .in6(R6), .in7(R7), .in8(R8), .in9(R9),
    .in10(R10), .in11(R11), .in12(R12), .in13(R13), .in14(R14), .in15(R15), .in16(R16), .in17(R17),
    .in18(R18), .in19(R19), .in20(R20), .in21(R21), .in22(R22), .in23(R23), .in24(R24), .in25(R25),
    .in26(R26), .in27(R27), .in28(R28), .in29(R29), .in30(R30), .in31(R31), .out(RTVALUE),
    .sel(INSTR_t[20:16]));
  Comparator #(.width(6), .mode("unsigned")) comparator_7 (
    .a(INSTR_t[31:26]), .b(6'b101011), .eq(IS_SW));  // open: gt, lt
  and and_25 (IS_SUB, IS_R, IS_SUB_F);
  Comparator #(.width(32), .mode("unsigned")) comparator_8 (.a(RSVALUE), .b(RTVALUE), .eq(EQ));  // open: gt, lt
  Multiplexer #(.width(32), .select(1), .enable("false")) multiplexer_7 (
    .in0(RSVALUE), .in1(RTVALUE), .out(ALUA), .sel(IS_SLL));
  Multiplexer #(.width(32), .select(1), .enable("false")) multiplexer_8 (
    .in0(ADDSUM), .in1(SUBSUM), .out(ADDSUB), .sel(ALUOP0));
  Multiplexer #(.width(32), .select(1), .enable("false")) multiplexer_9 (
    .in0(REGRESULT_BASE), .in1(LUI_VALUE), .out(REGRESULT), .sel(IS_LUI));
  Multiplexer #(.width(32), .select(1), .enable("false")) multiplexer_10 (
    .in0(PCBRANCH), .in1(JTARGET), .out(NEXTPC), .sel(IS_J));
  buf buffer_4 (MemWrite, IS_SW);
  ROM #(.addrWidth(12), .dataWidth(32)) rom_1 (.addr(PCINDEX), .data({INSTR_t, IMM16, FUNCT}), .sel(1'b1));
  Shifter #(.width(32), .shift("ll")) shifter_3 (.in(JINDEX32), .\dist (5'b00010), .out(JSHIFTED));
  and and_26 (EN0, DEC0, REGWE);
  and and_27 (EN3, DEC3, REGWE);
  and and_28 (EN6, DEC6, REGWE);
  and and_29 (EN9, DEC9, REGWE);
  and and_30 (EN12, DEC12, REGWE);
  and and_31 (EN15, DEC15, REGWE);
  and and_32 (EN18, DEC18, REGWE);
  and and_33 (EN21, DEC21, REGWE);
  and and_34 (EN24, DEC24, REGWE);
  and and_35 (EN27, DEC27, REGWE);
  and and_36 (EN30, DEC30, REGWE);
  Comparator #(.width(6), .mode("unsigned")) comparator_9 (
    .a(INSTR_t[31:26]), .b({6{1'b0}}), .eq(IS_R));  // open: gt, lt
  Comparator #(.width(6), .mode("unsigned")) comparator_10 (
    .a(INSTR_t[31:26]), .b(6'b000100), .eq(IS_BEQ));  // open: gt, lt
  and and_37 (IS_SLL, IS_R, IS_SLL_F);
  and and_38 (TAKEN, IS_BEQ, EQ);
  Multiplexer #(.width(32), .select(1), .enable("false")) multiplexer_11 (
    .in0(RTVALUE), .in1(IMMEXT), .out(ALUB), .sel(ALUSRC));
  Multiplexer #(.width(32), .select(1), .enable("false")) multiplexer_12 (
    .in0(OROUT), .in1(SLLOUT), .out(ALU_HI), .sel(ALUOP0));
  Shifter #(.width(32), .shift("ll")) shifter_4 (.in(SIGNIMM), .\dist (5'b00010), .out(SHIFTEDOFFSET));
  assign Instr = {INSTR_t, IMM16, FUNCT};  // Buffer buffer_5, 32 bits wide
  assign MemAddr = ALUOUT;  // Buffer buffer_6, 32 bits wide
  Multiplexer #(.width(5), .select(1), .enable("false")) multiplexer_13 (
    .in0(INSTR_t[20:16]), .in1(IMM16[15:11]), .out(WRITEADDR), .sel(IS_R));
  Register #(.width(32)) register_22 (.D(REGRESULT), .en(EN0), .Q(R0), .clk(CLKCPU), .clr(reset));
  Register #(.width(32)) register_23 (.D(REGRESULT), .en(EN3), .Q(R3), .clk(CLKCPU), .clr(reset));
  Register #(.width(32)) register_24 (.D(REGRESULT), .en(EN6), .Q(R6), .clk(CLKCPU), .clr(reset));
  Register #(.width(32)) register_25 (.D(REGRESULT), .en(EN9), .Q(R9), .clk(CLKCPU), .clr(reset));
  Register #(.width(32)) register_26 (.D(REGRESULT), .en(EN12), .Q(R12), .clk(CLKCPU), .clr(reset));
  Register #(.width(32)) register_27 (.D(REGRESULT), .en(EN15), .Q(R15), .clk(CLKCPU), .clr(reset));
  Register #(.width(32)) register_28 (.D(REGRESULT), .en(EN18), .Q(R18), .clk(CLKCPU), .clr(reset));
  Register #(.width(32)) register_29 (.D(REGRESULT), .en(EN21), .Q(R21), .clk(CLKCPU), .clr(reset));
  Register #(.width(32)) register_30 (.D(REGRESULT), .en(EN24), .Q(R24), .clk(CLKCPU), .clr(reset));
  Register #(.width(32)) register_31 (.D(REGRESULT), .en(EN27), .Q(R27), .clk(CLKCPU), .clr(reset));
  Register #(.width(32)) register_32 (.D(REGRESULT), .en(EN30), .Q(R30), .clk(CLKCPU), .clr(reset));
  Comparator #(.width(6), .mode("unsigned")) comparator_11 (
    .a(INSTR_t[31:26]), .b(6'b000010), .eq(IS_J));  // open: gt, lt
  Comparator #(.width(6), .mode("unsigned")) comparator_12 (.a(FUNCT), .b(6'b100000), .eq(IS_ADD_F));  // open: gt, lt
  or or_6 (REGWRITE_t, IS_ADD, IS_SUB, IS_SLL, IS_ORI, IS_LW, IS_LUI);
  assign SIGNIMM = {{16{IMM16[15]}}, {IMM16, FUNCT}};  // Bit_Extender bit_extender_3
  Adder #(.width(32)) adder_2 (.a(ALUA), .b(ALUB), .out(ADDSUM), .cin(1'b0));  // open: cout
  Multiplexer #(.width(32), .select(1), .enable("false")) multiplexer_14 (
    .in0(ADDSUB), .in1(ALU_HI), .out(ALUOUT), .sel(ALUOP1));
  Adder #(.width(32)) adder_3 (.a(PC4), .b(SHIFTEDOFFSET), .out(BRANCHTARGET), .cin(1'b0));  // open: cout
  assign pc = PC_t;  // Buffer buffer_7, 32 bits wide
  assign MemData = RTVALUE;  // Buffer buffer_8, 32 bits wide
  RAM #(.addrWidth(12), .dataWidth(32), .bus("separate")) UNUSED_RAM_0 ();  // open: addr, din, data, str, sel, clk, ld, clr
  RAM #(.addrWidth(12), .dataWidth(32), .bus("separate")) UNUSED_RAM_1 ();  // open: addr, din, data, str, sel, clk, ld, clr
  RAM #(.addrWidth(12), .dataWidth(32), .bus("separate")) UNUSED_RAM_2 ();  // open: addr, din, data, str, sel, clk, ld, clr

  // Other names for the same wires on the sheet: RAMADDR[11:0] = ALUOUT[13:2]; IMM16[5:0] = FUNCT;
  //   INSTR_t[15:0] = {IMM16, FUNCT}; JINDEX[25:0] = {INSTR_t[25:16], IMM16, FUNCT}; SHAMT[4:0] = IMM16[10:6];
  //   RD[4:0] = IMM16[15:11]; RT[4:0] = INSTR_t[20:16]; RS[4:0] = INSTR_t[25:21]; OPCODE[5:0] = INSTR_t[31:26];
  //   PCOFFSET[13:2] = PCINDEX
endmodule
