// Logisim project hierarchy.circ as structural Verilog: 2 circuits, main circuit HierarchicalCircuit
module CombinationalAdder (
  input  [7:0] A,
  input  [7:0] B,
  output [7:0] S
);

  Adder #(.width(8)) adder_1 (.a(A), .b(B), .out(S));  // open: cin, cout
endmodule

module HierarchicalCircuit (
  input  [7:0] A,
  input  [7:0] B,
  output [7:0] S
);

  CombinationalAdder combinationaladder_1 (.A(A), .B(B), .S(S));
endmodule
