// Logisim project logic-values.circ as structural Verilog: 1 circuit, main circuit LogicValues
module LogicValues (
  input  [7:0] X,
  output [7:0] U,
  output [7:0] E
);


  assign E = {8{1'b1}};
  assign U = X;
endmodule
