// Logisim project memory.circ as structural Verilog: 1 circuit, main circuit MemoryHarness
module MemoryHarness (
  input  [7:0] ADDR,
  input  CLK,
  input  RST,
  input  WE,
  input  OE,
  input  [31:0] DIN,
  output [31:0] DOUT,
  output [31:0] ROMOUT,
  output [31:0] Q
);

  ROM #(.addrWidth(8), .dataWidth(32)) rom_1 (.addr(ADDR), .data(ROMOUT), .sel(1'b1));
  RAM #(.addrWidth(8), .dataWidth(32), .bus("separate")) ram_1 (
    .addr(ADDR), .din(DIN), .data(DOUT), .str(WE), .sel(1'b1), .clk(CLK), .ld(OE), .clr(RST));
  Register #(.width(32)) PC (.D(DIN), .en(WE), .Q(Q), .clk(CLK), .clr(RST));
endmodule
