// Logisim project register.circ as structural Verilog: 1 circuit, main circuit Register
module Register (
  input  [7:0] D,
  input  WE,
  input  CLK,
  input  CLR,
  output [7:0] Q
);

  Register_part #(.width(8)) register_1 (.D(D), .en(WE), .Q(Q), .clk(CLK), .clr(CLR));
endmodule
